// Logisim project frisgotchi.circ as structural Verilog
module main (
);

  wire bit_extender_1_out, button_1_out, button_2_out, clock_1_out, multiplexer_1_out, not_1_out;
  wire [1:0] handler_1_out_6, handler_1_out_7, multiplexer_2_out;
  wire [31:0] handler_1_out_4, handler_1_out_5, idle_anim2_1__0, idle_anim2_1_out_2, idle_anim2_1_out_3,
       idle_anim2_1_out_4, idle_anim2_1_out_5, idle_anim2_1_out_7, idle_anim2_1_out_8, idle_anim2_1_out_9,
       idle_anim2_1_out_10, idle_anim2_1_out_11, idle_anim2_1_out_12, idle_anim2_1_out_13,
       idle_anim2_1_out_14, idle_anim2_1_out_15, idle_anim2_1_out_16, idle_anim2_1_out_17,
       idle_anim2_1_out_18, idle_anim2_1_out_19, idle_anim2_1_out_20, idle_anim2_1_out_21,
       idle_anim2_1_out_22, idle_anim2_1_out_23, idle_anim2_1_out_24, idle_anim2_1_out_25,
       idle_anim2_1_out_26, idle_anim2_1_out_27, idle_anim2_1_out_28, idle_anim2_1_out_29,
       idle_anim2_1_out_30, idle_anim2_1_out_31, idle_anim2_1_out_32, idle_anim2_1_out_33, idle_anim_1__0,
       idle_anim_1_out_2, idle_anim_1_out_3, idle_anim_1_out_4, idle_anim_1_out_5, idle_anim_1_out_7,
       idle_anim_1_out_8, idle_anim_1_out_9, idle_anim_1_out_10, idle_anim_1_out_11, idle_anim_1_out_12,
       idle_anim_1_out_13, idle_anim_1_out_14, idle_anim_1_out_15, idle_anim_1_out_16, idle_anim_1_out_17,
       idle_anim_1_out_18, idle_anim_1_out_19, idle_anim_1_out_20, idle_anim_1_out_21, idle_anim_1_out_22,
       idle_anim_1_out_23, idle_anim_1_out_24, idle_anim_1_out_25, idle_anim_1_out_26, idle_anim_1_out_27,
       idle_anim_1_out_28, idle_anim_1_out_29, idle_anim_1_out_30, idle_anim_1_out_31, idle_anim_1_out_32,
       idle_anim_1_out_33, selector_1_out_66, selector_1_out_67, selector_1_out_68, selector_1_out_69,
       selector_1_out_70, selector_1_out_71, selector_1_out_72, selector_1_out_73, selector_1_out_74,
       selector_1_out_75, selector_1_out_76, selector_1_out_77, selector_1_out_78, selector_1_out_79,
       selector_1_out_80, selector_1_out_81, selector_1_out_82, selector_1_out_83, selector_1_out_84,
       selector_1_out_85, selector_1_out_86, selector_1_out_87, selector_1_out_88, selector_1_out_89,
       selector_1_out_90, selector_1_out_91, selector_1_out_92, selector_1_out_93, selector_1_out_94,
       selector_1_out_95, selector_1_out_96, selector_1_out_97;

  Clock clock_1 (.out(clock_1_out));
  Multiplexer multiplexer_1 (
    .in0(clock_1_out), .in1(1'b0), .out(multiplexer_1_out), .sel(bit_extender_1_out));  // open: en
  Bit_Extender #(.in_width(2), .out_width(1), .\type ("one")) bit_extender_1 (
    .in(handler_1_out_7), .out(bit_extender_1_out));
  idle_anim idle_anim_1 (
    .in_1(multiplexer_2_out), .out_2(idle_anim_1_out_2), .out_3(idle_anim_1_out_3),
    .out_4(idle_anim_1_out_4), .out_5(idle_anim_1_out_5), ._0(idle_anim_1__0), .out_7(idle_anim_1_out_7),
    .out_8(idle_anim_1_out_8), .out_9(idle_anim_1_out_9), .out_10(idle_anim_1_out_10),
    .out_11(idle_anim_1_out_11), .out_12(idle_anim_1_out_12), .out_13(idle_anim_1_out_13),
    .out_14(idle_anim_1_out_14), .out_15(idle_anim_1_out_15), .out_16(idle_anim_1_out_16),
    .out_17(idle_anim_1_out_17), .out_18(idle_anim_1_out_18), .out_19(idle_anim_1_out_19),
    .out_20(idle_anim_1_out_20), .out_21(idle_anim_1_out_21), .out_22(idle_anim_1_out_22),
    .out_23(idle_anim_1_out_23), .out_24(idle_anim_1_out_24), .out_25(idle_anim_1_out_25),
    .out_26(idle_anim_1_out_26), .out_27(idle_anim_1_out_27), .out_28(idle_anim_1_out_28),
    .out_29(idle_anim_1_out_29), .out_30(idle_anim_1_out_30), .out_31(idle_anim_1_out_31),
    .out_32(idle_anim_1_out_32), .out_33(idle_anim_1_out_33));
  Multiplexer #(.width(2)) multiplexer_2 (
    .in0(handler_1_out_7), .in1(handler_1_out_6), .out(multiplexer_2_out), .sel(not_1_out));  // open: en
  not not_1 (not_1_out, bit_extender_1_out);
  Button button_1 (.out(button_1_out));
  Button button_2 (.out(button_2_out));
  DotMatrix #(.matrixcols(1), .matrixrows(32)) dotmatrix_1 (.col0(handler_1_out_4));
  DotMatrix #(.matrixcols(32), .matrixrows(32)) dotmatrix_2 (
    .col0(selector_1_out_66), .col1(selector_1_out_67), .col2(selector_1_out_68), .col3(selector_1_out_69),
    .col4(selector_1_out_70), .col5(selector_1_out_71), .col6(selector_1_out_72), .col7(selector_1_out_73),
    .col8(selector_1_out_74), .col9(selector_1_out_75), .col10(selector_1_out_76), .col11(selector_1_out_77),
    .col12(selector_1_out_78), .col13(selector_1_out_79), .col14(selector_1_out_80),
    .col15(selector_1_out_81), .col16(selector_1_out_82), .col17(selector_1_out_83),
    .col18(selector_1_out_84), .col19(selector_1_out_85), .col20(selector_1_out_86),
    .col21(selector_1_out_87), .col22(selector_1_out_88), .col23(selector_1_out_89),
    .col24(selector_1_out_90), .col25(selector_1_out_91), .col26(selector_1_out_92),
    .col27(selector_1_out_93), .col28(selector_1_out_94), .col29(selector_1_out_95),
    .col30(selector_1_out_96), .col31(selector_1_out_97));
  handler handler_1 (
    .feed_button(button_1_out), .sleep_button(button_2_out), .in_3(multiplexer_1_out),
    .out_4(handler_1_out_4), .out_5(handler_1_out_5), .out_7(handler_1_out_7), .out_6(handler_1_out_6));
  selector selector_1 (
    .in_1(multiplexer_1_out), .out_66(selector_1_out_66), .out_67(selector_1_out_67),
    .out_68(selector_1_out_68), .out_69(selector_1_out_69), .out_70(selector_1_out_70),
    .out_71(selector_1_out_71), .out_72(selector_1_out_72), .out_73(selector_1_out_73),
    .out_74(selector_1_out_74), .out_75(selector_1_out_75), .out_76(selector_1_out_76),
    .out_77(selector_1_out_77), .out_78(selector_1_out_78), .out_79(selector_1_out_79),
    .out_80(selector_1_out_80), .out_81(selector_1_out_81), .out_82(selector_1_out_82),
    .out_83(selector_1_out_83), .out_84(selector_1_out_84), .out_85(selector_1_out_85),
    .out_86(selector_1_out_86), .out_87(selector_1_out_87), .out_88(selector_1_out_88),
    .out_89(selector_1_out_89), .out_90(selector_1_out_90), .out_91(selector_1_out_91),
    .out_92(selector_1_out_92), .out_93(selector_1_out_93), .out_94(selector_1_out_94),
    .out_95(selector_1_out_95), .out_96(selector_1_out_96), .out_97(selector_1_out_97),
    .in_2(idle_anim_1_out_2), .in_3(idle_anim_1_out_3), .in_4(idle_anim_1_out_4), .in_5(idle_anim_1_out_5),
    .in_6(idle_anim_1__0), .in_7(idle_anim_1_out_7), .in_8(idle_anim_1_out_8), .in_9(idle_anim_1_out_9),
    .in_10(idle_anim_1_out_10), .in_11(idle_anim_1_out_11), .in_12(idle_anim_1_out_12),
    .in_13(idle_anim_1_out_13), .in_14(idle_anim_1_out_14), .in_15(idle_anim_1_out_15),
    .in_16(idle_anim_1_out_16), .in_17(idle_anim_1_out_17), .in_18(idle_anim_1_out_18),
    .in_19(idle_anim_1_out_19), .in_20(idle_anim_1_out_20), .in_21(idle_anim_1_out_21),
    .in_22(idle_anim_1_out_22), .in_23(idle_anim_1_out_23), .in_24(idle_anim_1_out_24),
    .in_25(idle_anim_1_out_25), .in_26(idle_anim_1_out_26), .in_27(idle_anim_1_out_27),
    .in_28(idle_anim_1_out_28), .in_29(idle_anim_1_out_29), .in_30(idle_anim_1_out_30),
    .in_31(idle_anim_1_out_31), .in_32(idle_anim_1_out_32), .in_33(idle_anim_1_out_33),
    .in_34(idle_anim2_1_out_2), .in_35(idle_anim2_1_out_3), .in_36(idle_anim2_1_out_4),
    .in_37(idle_anim2_1_out_5), .in_38(idle_anim2_1__0), .in_39(idle_anim2_1_out_7),
    .in_40(idle_anim2_1_out_8), .in_41(idle_anim2_1_out_9), .in_42(idle_anim2_1_out_10),
    .in_43(idle_anim2_1_out_11), .in_44(idle_anim2_1_out_12), .in_45(idle_anim2_1_out_13),
    .in_46(idle_anim2_1_out_14), .in_47(idle_anim2_1_out_15), .in_48(idle_anim2_1_out_16),
    .in_49(idle_anim2_1_out_17), .in_50(idle_anim2_1_out_18), .in_51(idle_anim2_1_out_19),
    .in_52(idle_anim2_1_out_20), .in_53(idle_anim2_1_out_21), .in_54(idle_anim2_1_out_22),
    .in_55(idle_anim2_1_out_23), .in_56(idle_anim2_1_out_24), .in_57(idle_anim2_1_out_25),
    .in_58(idle_anim2_1_out_26), .in_59(idle_anim2_1_out_27), .in_60(idle_anim2_1_out_28),
    .in_61(idle_anim2_1_out_29), .in_62(idle_anim2_1_out_30), .in_63(idle_anim2_1_out_31),
    .in_64(idle_anim2_1_out_32), .in_65(idle_anim2_1_out_33));
  DotMatrix #(.matrixcols(1), .matrixrows(32)) dotmatrix_3 (.col0(handler_1_out_5));
  idle_anim2 idle_anim2_1 (
    .out_2(idle_anim2_1_out_2), .out_3(idle_anim2_1_out_3), .out_4(idle_anim2_1_out_4),
    .out_5(idle_anim2_1_out_5), ._0(idle_anim2_1__0), .out_7(idle_anim2_1_out_7), .out_8(idle_anim2_1_out_8),
    .out_9(idle_anim2_1_out_9), .out_10(idle_anim2_1_out_10), .out_11(idle_anim2_1_out_11),
    .out_12(idle_anim2_1_out_12), .out_13(idle_anim2_1_out_13), .out_14(idle_anim2_1_out_14),
    .out_15(idle_anim2_1_out_15), .out_16(idle_anim2_1_out_16), .out_17(idle_anim2_1_out_17),
    .out_18(idle_anim2_1_out_18), .out_19(idle_anim2_1_out_19), .out_20(idle_anim2_1_out_20),
    .out_21(idle_anim2_1_out_21), .out_22(idle_anim2_1_out_22), .out_23(idle_anim2_1_out_23),
    .out_24(idle_anim2_1_out_24), .out_25(idle_anim2_1_out_25), .out_26(idle_anim2_1_out_26),
    .out_27(idle_anim2_1_out_27), .out_28(idle_anim2_1_out_28), .out_29(idle_anim2_1_out_29),
    .out_30(idle_anim2_1_out_30), .out_31(idle_anim2_1_out_31), .out_32(idle_anim2_1_out_32),
    .out_33(idle_anim2_1_out_33), .in_1(multiplexer_2_out));

  // Notes on the sheet:
  //   feed grass
  //   sleep
  //   hunger
  //   sleep
endmodule

module idle_anim (
  input  [1:0] in_1,
  output [31:0] out_2,
  output [31:0] out_3,
  output [31:0] out_4,
  output [31:0] out_5,
  output [31:0] _0,
  output [31:0] out_7,
  output [31:0] out_8,
  output [31:0] out_9,
  output [31:0] out_10,
  output [31:0] out_11,
  output [31:0] out_12,
  output [31:0] out_13,
  output [31:0] out_14,
  output [31:0] out_15,
  output [31:0] out_16,
  output [31:0] out_17,
  output [31:0] out_18,
  output [31:0] out_19,
  output [31:0] out_20,
  output [31:0] out_21,
  output [31:0] out_22,
  output [31:0] out_23,
  output [31:0] out_24,
  output [31:0] out_25,
  output [31:0] out_26,
  output [31:0] out_27,
  output [31:0] out_28,
  output [31:0] out_29,
  output [31:0] out_30,
  output [31:0] out_31,
  output [31:0] out_32,
  output [31:0] out_33
);

  Multiplexer #(.select(2), .width(32)) multiplexer_1 (
    .in0({32{1'b0}}), .in1({32{1'b0}}), .in2({32{1'b0}}), .in3({32{1'b0}}), .out(out_2), .sel(in_1));  // open: en
  Multiplexer #(.select(2), .width(32)) multiplexer_2 (
    .in0({32{1'b0}}), .in1({32{1'b0}}), .in2({32{1'b0}}), .in3({32{1'b0}}), .out(out_3), .sel(in_1));  // open: en
  Multiplexer #(.select(2), .width(32)) multiplexer_3 (
    .in0({32{1'b0}}), .in1(32'h700), .in2({32{1'b0}}), .in3({32{1'b0}}), .out(out_4), .sel(in_1));  // open: en
  Multiplexer #(.select(2), .width(32)) multiplexer_4 (
    .in0({32{1'b0}}), .in1(32'h20c0), .in2({32{1'b0}}), .in3({32{1'b0}}), .out(out_5), .sel(in_1));  // open: en
  Multiplexer #(.select(2), .width(32)) multiplexer_5 (
    .in0({32{1'b0}}), .in1(32'h1f00), .in2({32{1'b0}}), .in3({32{1'b0}}), .out(_0), .sel(in_1));  // open: en
  Multiplexer #(.select(2), .width(32)) multiplexer_6 (
    .in0({32{1'b0}}), .in1(32'h880), .in2({32{1'b0}}), .in3({32{1'b0}}), .out(out_7), .sel(in_1));  // open: en
  Multiplexer #(.select(2), .width(32)) multiplexer_7 (
    .in0({32{1'b0}}), .in1(32'h1f040), .in2(32'hf00), .in3({32{1'b0}}), .out(out_8), .sel(in_1));  // open: en
  Multiplexer #(.select(2), .width(32)) multiplexer_8 (
    .in0(32'h1e000), .in1(32'h209c0), .in2(32'h3080), .in3({32{1'b0}}), .out(out_9), .sel(in_1));  // open: en
  Multiplexer #(.select(2), .width(32)) multiplexer_9 (
    .in0(32'h61000), .in1(32'he40680), .in2(32'h4040), .in3({32{1'b0}}), .out(out_10), .sel(in_1));  // open: en
  Multiplexer #(.select(2), .width(32)) multiplexer_10 (
    .in0(32'h1c80800), .in1(32'h11c0400), .in2(32'h1c040), .in3({32{1'b0}}), .out(out_11), .sel(in_1));  // open: en
  Multiplexer #(.select(2), .width(32)) multiplexer_11 (
    .in0(32'h2380800), .in1(32'h1042480), .in2(32'h24240), .in3({32{1'b0}}), .out(out_12), .sel(in_1));  // open: en
  Multiplexer #(.select(2), .width(32)) multiplexer_12 (
    .in0(32'h208c880), .in1(32'h982740), .in2(32'h48240), .in3({32{1'b0}}), .out(out_13), .sel(in_1));  // open: en
  Multiplexer #(.select(2), .width(32)) multiplexer_13 (
    .in0(32'h1900740), .in1(32'h600040), .in2(32'h70040), .in3({32{1'b0}}), .out(out_14), .sel(in_1));  // open: en
  Multiplexer #(.select(2), .width(32)) multiplexer_14 (
    .in0(32'h600040), .in1(32'h840040), .in2(32'hc4040), .in3({32{1'b0}}), .out(out_15), .sel(in_1));  // open: en
  Multiplexer #(.select(2), .width(32)) multiplexer_15 (
    .in0(32'h1880040), .in1(32'h10c0180), .in2(32'h104080), .in3({32{1'b0}}), .out(out_16), .sel(in_1));  // open: en
  Multiplexer #(.select(2), .width(32)) multiplexer_16 (
    .in0(32'h2080180), .in1(32'h1120240), .in2(32'h108040), .in3({32{1'b0}}), .out(out_17), .sel(in_1));  // open: en
  Multiplexer #(.select(2), .width(32)) multiplexer_17 (
    .in0(32'h2160240), .in1(32'he10040), .in2(32'hf0040), .in3({32{1'b0}}), .out(out_18), .sel(in_1));  // open: en
  Multiplexer #(.select(2), .width(32)) multiplexer_18 (
    .in0(32'h1e10040), .in1(32'h10040), .in2(32'h8040), .in3({32{1'b0}}), .out(out_19), .sel(in_1));  // open: en
  Multiplexer #(.select(2), .width(32)) multiplexer_19 (
    .in0(32'h10040), .in1(32'h10080), .in2(32'h208080), .in3({32{1'b0}}), .out(out_20), .sel(in_1));  // open: en
  Multiplexer #(.select(2), .width(32)) multiplexer_20 (
    .in0(32'h10080), .in1(32'h8040), .in2(32'h408040), .in3({32{1'b0}}), .out(out_21), .sel(in_1));  // open: en
  Multiplexer #(.select(2), .width(32)) multiplexer_21 (
    .in0(32'h8040), .in1(32'h8180), .in2(32'h588080), .in3({32{1'b0}}), .out(out_22), .sel(in_1));  // open: en
  Multiplexer #(.select(2), .width(32)) multiplexer_22 (
    .in0(32'h8180), .in1(32'h8040), .in2(32'h2684040), .in3({32{1'b0}}), .out(out_23), .sel(in_1));  // open: en
  Multiplexer #(.select(2), .width(32)) multiplexer_23 (
    .in0(32'h8040), .in1(32'h8040), .in2(32'h4104040), .in3({32{1'b0}}), .out(out_24), .sel(in_1));  // open: en
  Multiplexer #(.select(2), .width(32)) multiplexer_24 (
    .in0(32'h8040), .in1(32'h4080), .in2(32'h5a02040), .in3({32{1'b0}}), .out(out_25), .sel(in_1));  // open: en
  Multiplexer #(.select(2), .width(32)) multiplexer_25 (
    .in0(32'h4080), .in1(32'h3f00), .in2(32'h6801f80), .in3({32{1'b0}}), .out(out_26), .sel(in_1));  // open: en
  Multiplexer #(.select(2), .width(32)) multiplexer_26 (
    .in0(32'h3f00), .in1({32{1'b0}}), .in2(32'h1000000), .in3({32{1'b0}}), .out(out_27), .sel(in_1));  // open: en
  Multiplexer #(.select(2), .width(32)) multiplexer_27 (
    .in0({32{1'b0}}), .in1({32{1'b0}}), .in2({32{1'b0}}), .in3({32{1'b0}}), .out(out_28), .sel(in_1));  // open: en
  Multiplexer #(.select(2), .width(32)) multiplexer_28 (
    .in0({32{1'b0}}), .in1({32{1'b0}}), .in2({32{1'b0}}), .in3({32{1'b0}}), .out(out_29), .sel(in_1));  // open: en
  Multiplexer #(.select(2), .width(32)) multiplexer_29 (
    .in0({32{1'b0}}), .in1({32{1'b0}}), .in2({32{1'b0}}), .in3({32{1'b0}}), .out(out_30), .sel(in_1));  // open: en
  Multiplexer #(.select(2), .width(32)) multiplexer_30 (
    .in0({32{1'b0}}), .in1({32{1'b0}}), .in2({32{1'b0}}), .in3({32{1'b0}}), .out(out_31), .sel(in_1));  // open: en
  Multiplexer #(.select(2), .width(32)) multiplexer_31 (
    .in0({32{1'b0}}), .in1({32{1'b0}}), .in2({32{1'b0}}), .in3({32{1'b0}}), .out(out_32), .sel(in_1));  // open: en
  Multiplexer #(.select(2), .width(32)) multiplexer_32 (
    .in0({32{1'b0}}), .in1({32{1'b0}}), .in2({32{1'b0}}), .in3({32{1'b0}}), .out(out_33), .sel(in_1));  // open: en
endmodule

module selector (
  input  in_1,
  input  [31:0] in_2,
  input  [31:0] in_3,
  input  [31:0] in_4,
  input  [31:0] in_5,
  input  [31:0] in_6,
  input  [31:0] in_7,
  input  [31:0] in_8,
  input  [31:0] in_9,
  input  [31:0] in_10,
  input  [31:0] in_11,
  input  [31:0] in_12,
  input  [31:0] in_13,
  input  [31:0] in_14,
  input  [31:0] in_15,
  input  [31:0] in_16,
  input  [31:0] in_17,
  input  [31:0] in_18,
  input  [31:0] in_19,
  input  [31:0] in_20,
  input  [31:0] in_21,
  input  [31:0] in_22,
  input  [31:0] in_23,
  input  [31:0] in_24,
  input  [31:0] in_25,
  input  [31:0] in_26,
  input  [31:0] in_27,
  input  [31:0] in_28,
  input  [31:0] in_29,
  input  [31:0] in_30,
  input  [31:0] in_31,
  input  [31:0] in_32,
  input  [31:0] in_33,
  input  [31:0] in_34,
  input  [31:0] in_35,
  input  [31:0] in_36,
  input  [31:0] in_37,
  input  [31:0] in_38,
  input  [31:0] in_39,
  input  [31:0] in_40,
  input  [31:0] in_41,
  input  [31:0] in_42,
  input  [31:0] in_43,
  input  [31:0] in_44,
  input  [31:0] in_45,
  input  [31:0] in_46,
  input  [31:0] in_47,
  input  [31:0] in_48,
  input  [31:0] in_49,
  input  [31:0] in_50,
  input  [31:0] in_51,
  input  [31:0] in_52,
  input  [31:0] in_53,
  input  [31:0] in_54,
  input  [31:0] in_55,
  input  [31:0] in_56,
  input  [31:0] in_57,
  input  [31:0] in_58,
  input  [31:0] in_59,
  input  [31:0] in_60,
  input  [31:0] in_61,
  input  [31:0] in_62,
  input  [31:0] in_63,
  input  [31:0] in_64,
  input  [31:0] in_65,
  output [31:0] out_66,
  output [31:0] out_67,
  output [31:0] out_68,
  output [31:0] out_69,
  output [31:0] out_70,
  output [31:0] out_71,
  output [31:0] out_72,
  output [31:0] out_73,
  output [31:0] out_74,
  output [31:0] out_75,
  output [31:0] out_76,
  output [31:0] out_77,
  output [31:0] out_78,
  output [31:0] out_79,
  output [31:0] out_80,
  output [31:0] out_81,
  output [31:0] out_82,
  output [31:0] out_83,
  output [31:0] out_84,
  output [31:0] out_85,
  output [31:0] out_86,
  output [31:0] out_87,
  output [31:0] out_88,
  output [31:0] out_89,
  output [31:0] out_90,
  output [31:0] out_91,
  output [31:0] out_92,
  output [31:0] out_93,
  output [31:0] out_94,
  output [31:0] out_95,
  output [31:0] out_96,
  output [31:0] out_97
);

  Multiplexer #(.width(32)) multiplexer_1 (.in0(in_2), .in1(in_34), .out(out_66), .sel(in_1));  // open: en
  Multiplexer #(.width(32)) multiplexer_2 (.in0(in_3), .in1(in_35), .out(out_67), .sel(in_1));  // open: en
  Multiplexer #(.width(32)) multiplexer_3 (.in0(in_5), .in1(in_37), .out(out_69), .sel(in_1));  // open: en
  Multiplexer #(.width(32)) multiplexer_4 (.in0(in_4), .in1(in_36), .out(out_68), .sel(in_1));  // open: en
  Multiplexer #(.width(32)) multiplexer_5 (.in0(in_6), .in1(in_38), .out(out_70), .sel(in_1));  // open: en
  Multiplexer #(.width(32)) multiplexer_6 (.in0(in_8), .in1(in_40), .out(out_72), .sel(in_1));  // open: en
  Multiplexer #(.width(32)) multiplexer_7 (.in0(in_7), .in1(in_39), .out(out_71), .sel(in_1));  // open: en
  Multiplexer #(.width(32)) multiplexer_8 (.in0(in_10), .in1(in_42), .out(out_74), .sel(in_1));  // open: en
  Multiplexer #(.width(32)) multiplexer_9 (.in0(in_9), .in1(in_41), .out(out_73), .sel(in_1));  // open: en
  Multiplexer #(.width(32)) multiplexer_10 (.in0(in_11), .in1(in_43), .out(out_75), .sel(in_1));  // open: en
  Multiplexer #(.width(32)) multiplexer_11 (.in0(in_13), .in1(in_45), .out(out_77), .sel(in_1));  // open: en
  Multiplexer #(.width(32)) multiplexer_12 (.in0(in_12), .in1(in_44), .out(out_76), .sel(in_1));  // open: en
  Multiplexer #(.width(32)) multiplexer_13 (.in0(in_14), .in1(in_46), .out(out_78), .sel(in_1));  // open: en
  Multiplexer #(.width(32)) multiplexer_14 (.in0(in_16), .in1(in_48), .out(out_80), .sel(in_1));  // open: en
  Multiplexer #(.width(32)) multiplexer_15 (.in0(in_15), .in1(in_47), .out(out_79), .sel(in_1));  // open: en
  Multiplexer #(.width(32)) multiplexer_16 (.in0(in_18), .in1(in_50), .out(out_82), .sel(in_1));  // open: en
  Multiplexer #(.width(32)) multiplexer_17 (.in0(in_17), .in1(in_49), .out(out_81), .sel(in_1));  // open: en
  Multiplexer #(.width(32)) multiplexer_18 (.in0(in_19), .in1(in_51), .out(out_83), .sel(in_1));  // open: en
  Multiplexer #(.width(32)) multiplexer_19 (.in0(in_20), .in1(in_52), .out(out_84), .sel(in_1));  // open: en
  Multiplexer #(.width(32)) multiplexer_20 (.in0(in_21), .in1(in_53), .out(out_85), .sel(in_1));  // open: en
  Multiplexer #(.width(32)) multiplexer_21 (.in0(in_22), .in1(in_54), .out(out_86), .sel(in_1));  // open: en
  Multiplexer #(.width(32)) multiplexer_22 (.in0(in_24), .in1(in_56), .out(out_88), .sel(in_1));  // open: en
  Multiplexer #(.width(32)) multiplexer_23 (.in0(in_23), .in1(in_55), .out(out_87), .sel(in_1));  // open: en
  Multiplexer #(.width(32)) multiplexer_24 (.in0(in_26), .in1(in_58), .out(out_90), .sel(in_1));  // open: en
  Multiplexer #(.width(32)) multiplexer_25 (.in0(in_25), .in1(in_57), .out(out_89), .sel(in_1));  // open: en
  Multiplexer #(.width(32)) multiplexer_26 (.in0(in_27), .in1(in_59), .out(out_91), .sel(in_1));  // open: en
  Multiplexer #(.width(32)) multiplexer_27 (.in0(in_29), .in1(in_61), .out(out_93), .sel(in_1));  // open: en
  Multiplexer #(.width(32)) multiplexer_28 (.in0(in_28), .in1(in_60), .out(out_92), .sel(in_1));  // open: en
  Multiplexer #(.width(32)) multiplexer_29 (.in0(in_30), .in1(in_62), .out(out_94), .sel(in_1));  // open: en
  Multiplexer #(.width(32)) multiplexer_30 (.in0(in_32), .in1(in_64), .out(out_96), .sel(in_1));  // open: en
  Multiplexer #(.width(32)) multiplexer_31 (.in0(in_31), .in1(in_63), .out(out_95), .sel(in_1));  // open: en
  Multiplexer #(.width(32)) multiplexer_32 (.in0(in_33), .in1(in_65), .out(out_97), .sel(in_1));  // open: en
endmodule

module idle_anim2 (
  input  [1:0] in_1,
  output [31:0] out_2,
  output [31:0] out_3,
  output [31:0] out_4,
  output [31:0] out_5,
  output [31:0] _0,
  output [31:0] out_7,
  output [31:0] out_8,
  output [31:0] out_9,
  output [31:0] out_10,
  output [31:0] out_11,
  output [31:0] out_12,
  output [31:0] out_13,
  output [31:0] out_14,
  output [31:0] out_15,
  output [31:0] out_16,
  output [31:0] out_17,
  output [31:0] out_18,
  output [31:0] out_19,
  output [31:0] out_20,
  output [31:0] out_21,
  output [31:0] out_22,
  output [31:0] out_23,
  output [31:0] out_24,
  output [31:0] out_25,
  output [31:0] out_26,
  output [31:0] out_27,
  output [31:0] out_28,
  output [31:0] out_29,
  output [31:0] out_30,
  output [31:0] out_31,
  output [31:0] out_32,
  output [31:0] out_33
);

  Multiplexer #(.select(2), .width(32)) multiplexer_1 (
    .in0({32{1'b0}}), .in1({32{1'b0}}), .in2({32{1'b0}}), .in3({32{1'b0}}), .out(out_2), .sel(in_1));  // open: en
  Multiplexer #(.select(2), .width(32)) multiplexer_2 (
    .in0({32{1'b0}}), .in1({32{1'b0}}), .in2({32{1'b0}}), .in3({32{1'b0}}), .out(out_3), .sel(in_1));  // open: en
  Multiplexer #(.select(2), .width(32)) multiplexer_3 (
    .in0({32{1'b0}}), .in1(32'h300), .in2({32{1'b0}}), .in3({32{1'b0}}), .out(out_4), .sel(in_1));  // open: en
  Multiplexer #(.select(2), .width(32)) multiplexer_4 (
    .in0({32{1'b0}}), .in1(32'hc0), .in2({32{1'b0}}), .in3({32{1'b0}}), .out(out_5), .sel(in_1));  // open: en
  Multiplexer #(.select(2), .width(32)) multiplexer_5 (
    .in0({32{1'b0}}), .in1(32'h300), .in2({32{1'b0}}), .in3({32{1'b0}}), .out(_0), .sel(in_1));  // open: en
  Multiplexer #(.select(2), .width(32)) multiplexer_6 (
    .in0({32{1'b0}}), .in1(32'h480), .in2({32{1'b0}}), .in3({32{1'b0}}), .out(out_7), .sel(in_1));  // open: en
  Multiplexer #(.select(2), .width(32)) multiplexer_7 (
    .in0(32'h40f000), .in1(32'h1e040), .in2(32'hf00), .in3({32{1'b0}}), .out(out_8), .sel(in_1));  // open: en
  Multiplexer #(.select(2), .width(32)) multiplexer_8 (
    .in0(32'ha30800), .in1(32'h61180), .in2(32'h3080), .in3({32{1'b0}}), .out(out_9), .sel(in_1));  // open: en
  Multiplexer #(.select(2), .width(32)) multiplexer_9 (
    .in0(32'ha40400), .in1(32'h1c80a00), .in2(32'h4040), .in3({32{1'b0}}), .out(out_10), .sel(in_1));  // open: en
  Multiplexer #(.select(2), .width(32)) multiplexer_10 (
    .in0(32'h980480), .in1(32'h2380c00), .in2(32'h1c040), .in3({32{1'b0}}), .out(out_11), .sel(in_1));  // open: en
  Multiplexer #(.select(2), .width(32)) multiplexer_11 (
    .in0(32'h886540), .in1(32'h2084880), .in2(32'h24240), .in3({32{1'b0}}), .out(out_12), .sel(in_1));  // open: en
  Multiplexer #(.select(2), .width(32)) multiplexer_12 (
    .in0(32'h500240), .in1(32'h1904740), .in2(32'h48240), .in3({32{1'b0}}), .out(out_13), .sel(in_1));  // open: en
  Multiplexer #(.select(2), .width(32)) multiplexer_13 (
    .in0(32'h200040), .in1(32'h600040), .in2(32'h70040), .in3({32{1'b0}}), .out(out_14), .sel(in_1));  // open: en
  Multiplexer #(.select(2), .width(32)) multiplexer_14 (
    .in0(32'h480080), .in1(32'h1880040), .in2(32'h44040), .in3({32{1'b0}}), .out(out_15), .sel(in_1));  // open: en
  Multiplexer #(.select(2), .width(32)) multiplexer_15 (
    .in0(32'h480100), .in1(32'h2080180), .in2(32'h84080), .in3({32{1'b0}}), .out(out_16), .sel(in_1));  // open: en
  Multiplexer #(.select(2), .width(32)) multiplexer_16 (
    .in0(32'h960280), .in1(32'h2160240), .in2(32'h108040), .in3({32{1'b0}}), .out(out_17), .sel(in_1));  // open: en
  Multiplexer #(.select(2), .width(32)) multiplexer_17 (
    .in0(32'h910040), .in1(32'h1e10040), .in2(32'h110040), .in3({32{1'b0}}), .out(out_18), .sel(in_1));  // open: en
  Multiplexer #(.select(2), .width(32)) multiplexer_18 (
    .in0(32'h910040), .in1(32'h10040), .in2(32'he8040), .in3({32{1'b0}}), .out(out_19), .sel(in_1));  // open: en
  Multiplexer #(.select(2), .width(32)) multiplexer_19 (
    .in0(32'ha10080), .in1(32'h10080), .in2(32'h408080), .in3({32{1'b0}}), .out(out_20), .sel(in_1));  // open: en
  Multiplexer #(.select(2), .width(32)) multiplexer_20 (
    .in0(32'h408100), .in1(32'h8040), .in2(32'h808040), .in3({32{1'b0}}), .out(out_21), .sel(in_1));  // open: en
  Multiplexer #(.select(2), .width(32)) multiplexer_21 (
    .in0(32'h8080), .in1(32'h8180), .in2(32'hb08080), .in3({32{1'b0}}), .out(out_22), .sel(in_1));  // open: en
  Multiplexer #(.select(2), .width(32)) multiplexer_22 (
    .in0(32'h8040), .in1(32'h8040), .in2(32'hd04040), .in3({32{1'b0}}), .out(out_23), .sel(in_1));  // open: en
  Multiplexer #(.select(2), .width(32)) multiplexer_23 (
    .in0(32'h4040), .in1(32'h8040), .in2(32'h4204040), .in3({32{1'b0}}), .out(out_24), .sel(in_1));  // open: en
  Multiplexer #(.select(2), .width(32)) multiplexer_24 (
    .in0(32'h2040), .in1(32'h4080), .in2(32'h8402040), .in3({32{1'b0}}), .out(out_25), .sel(in_1));  // open: en
  Multiplexer #(.select(2), .width(32)) multiplexer_25 (
    .in0(32'h1f80), .in1(32'h3f00), .in2(32'hb001f80), .in3({32{1'b0}}), .out(out_26), .sel(in_1));  // open: en
  Multiplexer #(.select(2), .width(32)) multiplexer_26 (
    .in0({32{1'b0}}), .in1({32{1'b0}}), .in2(32'hd000000), .in3({32{1'b0}}), .out(out_27), .sel(in_1));  // open: en
  Multiplexer #(.select(2), .width(32)) multiplexer_27 (
    .in0({32{1'b0}}), .in1({32{1'b0}}), .in2(32'h2000000), .in3({32{1'b0}}), .out(out_28), .sel(in_1));  // open: en
  Multiplexer #(.select(2), .width(32)) multiplexer_28 (
    .in0({32{1'b0}}), .in1({32{1'b0}}), .in2({32{1'b0}}), .in3({32{1'b0}}), .out(out_29), .sel(in_1));  // open: en
  Multiplexer #(.select(2), .width(32)) multiplexer_29 (
    .in0({32{1'b0}}), .in1({32{1'b0}}), .in2({32{1'b0}}), .in3({32{1'b0}}), .out(out_30), .sel(in_1));  // open: en
  Multiplexer #(.select(2), .width(32)) multiplexer_30 (
    .in0({32{1'b0}}), .in1({32{1'b0}}), .in2({32{1'b0}}), .in3({32{1'b0}}), .out(out_31), .sel(in_1));  // open: en
  Multiplexer #(.select(2), .width(32)) multiplexer_31 (
    .in0({32{1'b0}}), .in1({32{1'b0}}), .in2({32{1'b0}}), .in3({32{1'b0}}), .out(out_32), .sel(in_1));  // open: en
  Multiplexer #(.select(2), .width(32)) multiplexer_32 (
    .in0({32{1'b0}}), .in1({32{1'b0}}), .in2({32{1'b0}}), .in3({32{1'b0}}), .out(out_33), .sel(in_1));  // open: en
endmodule

module hunger (
  input  in_1,
  input  in_2,
  output [31:0] out_3,
  output out_4
);

  wire d_ff_1_q, d_ff_2_q, not_1_out, not_2_out, not_3_out, or_1_out;
  wire [4:0] counter_1_q;
  wire [31:0] shifter_1_out;

  Shifter #(.width(32), .shift("ar")) shifter_1 (.in(32'h80000000), .\dist (counter_1_q), .out(shifter_1_out));
  Counter #(.width(5), .max('h1f), .ongoal("stay")) counter_1 (
    .Q(counter_1_q), .clk(d_ff_1_q), .clr(in_1));  // open: load, D, count, carry
  not not_1 (not_1_out, d_ff_1_q);
  D_Flip_Flop d_ff_1 (.clk(in_2), .D(not_1_out), .Q(d_ff_1_q));  // open: Qn, preset, en, reset
  D_Flip_Flop d_ff_2 (.clk(d_ff_1_q), .D(d_ff_1_q), .Q(d_ff_2_q));  // open: Qn, preset, en, reset
  Multiplexer #(.width(32)) multiplexer_1 (
    .in0({32{1'b0}}), .in1(shifter_1_out), .out(out_3), .sel(not_2_out));  // open: en
  not not_2 (not_2_out, or_1_out);
  or or_1 (or_1_out, in_1, not_3_out);
  not not_3 (not_3_out, d_ff_2_q);
  Comparator #(.width(32)) comparator_1 (.a(out_3), .b({32{1'b1}}), .eq(out_4));  // open: gt, lt
endmodule

module sleep (
  input  in_1,
  input  in_2,
  output [31:0] out_3,
  output out_4
);

  wire d_ff_1_q, d_ff_2_q, d_ff_3_q, d_ff_4_q, d_ff_5_q, not_1_out, not_2_out, not_3_out, not_4_out,
       not_5_out, not_6_out, or_1_out;
  wire [4:0] counter_1_q;
  wire [31:0] shifter_1_out;

  not not_1 (not_1_out, d_ff_1_q);
  D_Flip_Flop d_ff_1 (.clk(in_2), .D(not_1_out), .Q(d_ff_1_q));  // open: Qn, preset, en, reset
  not not_2 (not_2_out, d_ff_2_q);
  D_Flip_Flop d_ff_2 (.clk(d_ff_1_q), .D(not_2_out), .Q(d_ff_2_q));  // open: Qn, preset, en, reset
  not not_3 (not_3_out, d_ff_3_q);
  Shifter #(.width(32), .shift("ar")) shifter_1 (.in(32'h80000000), .\dist (counter_1_q), .out(shifter_1_out));
  Counter #(.width(5), .max('h1f), .ongoal("stay")) counter_1 (
    .Q(counter_1_q), .clk(d_ff_4_q), .clr(in_1));  // open: load, D, count, carry
  D_Flip_Flop d_ff_3 (.clk(d_ff_2_q), .D(not_3_out), .Q(d_ff_3_q));  // open: Qn, preset, en, reset
  not not_4 (not_4_out, d_ff_4_q);
  D_Flip_Flop d_ff_4 (.clk(d_ff_3_q), .D(not_4_out), .Q(d_ff_4_q));  // open: Qn, preset, en, reset
  D_Flip_Flop d_ff_5 (.clk(d_ff_4_q), .D(d_ff_4_q), .Q(d_ff_5_q));  // open: Qn, preset, en, reset
  Multiplexer #(.width(32)) multiplexer_1 (
    .in0({32{1'b0}}), .in1(shifter_1_out), .out(out_3), .sel(not_5_out));  // open: en
  not not_5 (not_5_out, or_1_out);
  or or_1 (or_1_out, in_1, not_6_out);
  not not_6 (not_6_out, d_ff_5_q);
  Comparator #(.width(32)) comparator_1 (.a(out_3), .b({32{1'b1}}), .eq(out_4));  // open: gt, lt
endmodule

module handler (
  input  feed_button,
  input  sleep_button,
  input  in_3,
  output [31:0] out_4,
  output [31:0] out_5,
  output [1:0] out_6,
  output [1:0] out_7
);

  wire hunger_1_out_4, or_1_out, sleep_1_out_4;

  hunger hunger_1 (.in_1(feed_button), .in_2(in_3), .out_3(out_4), .out_4(hunger_1_out_4));
  sleep sleep_1 (.in_1(sleep_button), .in_2(in_3), .out_3(out_5), .out_4(sleep_1_out_4));
  or or_1 (or_1_out, sleep_1_out_4, hunger_1_out_4);
  Multiplexer #(.width(2)) multiplexer_1 (.in0(2'b00), .in1(2'b11), .out(out_7), .sel(or_1_out));  // open: en
  Multiplexer #(.select(2), .width(2)) multiplexer_2 (
    .in0(2'b00), .in1(2'b01), .in2(2'b10), .in3(2'b11), .out(out_6), .sel({sleep_button, feed_button}));  // open: en
endmodule
